// Logisim project project.circ as structural Verilog: 1 circuit, main circuit main
module main (
  input  a,
  input  b,
  input  c,
  input  c_2,
  input  b_2,
  input  a_2,
  input  b_3,
  input  c_3,
  input  b_4,
  input  c_4,
  output out_11
);

  wire and_1_out, and_2_out, and_3_out, and_4_out, and_5_out, and_6_out, not_1_out, not_2_out, not_3_out,
       not_4_out, not_5_out, or_1_out, or_2_out;

  not not_1 (not_1_out, a);
  not not_2 (not_2_out, b);
  not not_3 (not_3_out, c);
  not not_4 (not_4_out, b_3);
  not not_5 (not_5_out, c_4);
  and and_1 (and_1_out, c_2, b_2);
  and and_2 (and_2_out, not_2_out, not_3_out);
  and and_3 (and_3_out, not_4_out, c_3);
  and and_4 (and_4_out, b_4, not_5_out);
  or or_1 (or_1_out, and_3_out, and_4_out);
  or or_2 (or_2_out, and_2_out, and_1_out);
  and and_5 (and_5_out, not_1_out, or_2_out);
  and and_6 (and_6_out, a_2, or_1_out);
  or or_3 (out_11, and_5_out, and_6_out);
endmodule
