// Logisim project project.circ as structural Verilog: 4 circuits, main circuit main
module main (
  input  a,
  input  b,
  input  c,
  input  d,
  output d1,
  output d0
);

  deciding_mechanism deciding_mechanism_1 (.a(a), .b(b), .c(c), .d(d), .d1(d1), .d0(d0));
endmodule

module first (
  input  a,
  input  b,
  input  d,
  input  c,
  output out_5
);

  wire and_1_out, not_1_out, not_2_out, not_3_out;

  not not_1 (not_1_out, a);
  not not_2 (not_2_out, b);
  not not_3 (not_3_out, d);
  and and_1 (and_1_out, not_1_out, not_2_out, not_3_out);
  or or_1 (out_5, and_1_out, c);
endmodule

module second (
  input  a,
  input  b,
  input  c,
  input  d,
  output out_5
);

  wire and_1_out, not_1_out, not_2_out, not_3_out;

  not not_1 (not_1_out, a);
  not not_2 (not_2_out, b);
  not not_3 (not_3_out, c);
  and and_1 (and_1_out, not_1_out, not_2_out, not_3_out);
  or or_1 (out_5, and_1_out, d);
endmodule

module deciding_mechanism (
  input  a,
  input  b,
  input  c,
  input  d,
  output d1,
  output d0
);

  first first_1 (.a(a), .b(b), .d(d), .c(c), .out_5(d1));
  second second_1 (.a(a), .b(b), .c(c), .d(d), .out_5(d0));
endmodule
