// Logisim project project.circ as structural Verilog: 3 circuits, main circuit main
module main (
  input  a,
  input  b,
  output x
);

  wire combinational_logic_part_1_n0, combinational_logic_part_1_n1, n2_bit_register_part_1_s0,
       n2_bit_register_part_1_s1;

  Combinational_Logic_Part combinational_logic_part_1 (
    .C(n2_bit_register_part_1_s1), .D(n2_bit_register_part_1_s0), .a(a), .b(b), .x(x),
    .n1(combinational_logic_part_1_n1), .n0(combinational_logic_part_1_n0));
  _2_bit_Register_Part u_2_bit_register_part_1 (
    .s1(n2_bit_register_part_1_s1), .s0(n2_bit_register_part_1_s0), .n1(combinational_logic_part_1_n1),
    .n0(combinational_logic_part_1_n0));
endmodule

module Combinational_Logic_Part (
  input  C,
  input  D,
  input  a,
  input  b,
  output x,
  output n1,
  output n0
);

  wire and_1_out, and_2_out, and_3_out, and_4_out, and_5_out, and_6_out, not_1_out, not_2_out, not_3_out,
       not_4_out;

  not not_1 (not_1_out, C);
  not not_2 (not_2_out, D);
  not not_3 (not_3_out, a);
  not not_4 (not_4_out, b);
  and and_1 (and_1_out, C, b);
  and and_2 (and_2_out, not_1_out, D, a);
  and and_3 (and_3_out, C, not_2_out, not_3_out);
  and and_4 (and_4_out, C, D, b);
  and and_5 (and_5_out, not_1_out, a, not_4_out);
  and and_6 (and_6_out, C, not_3_out, b);
  or or_1 (n1, and_1_out, and_2_out, and_3_out);
  or or_2 (n0, and_4_out, and_5_out, and_6_out);

  assign x = C;
endmodule

module _2_bit_Register_Part (
  input  n1,
  input  n0,
  output s1,
  output s0
);

  wire clock_1_out;

  Clock clock_1 (.out(clock_1_out));
  D_Flip_Flop d_ff_1 (.clk(clock_1_out), .D(n1), .Q(s1), .en(1'b1));  // open: Qn, preset, reset
  D_Flip_Flop d_ff_2 (.clk(clock_1_out), .D(n0), .Q(s0), .en(1'b1));  // open: Qn, preset, reset
endmodule
