// Logisim project project.circ as structural Verilog: 3 circuits, main circuit main
module main (
  input  req,
  input  p3s,
  input  p7s,
  input  p37s,
  output resetT
);

  wire controller_1_n0, controller_1_n1, controller_1_n1_2, controller_1_org, controller_1_red,
       register_1_s0, register_1_s1;

  controller controller_1 (
    .s1(register_1_s1), .s0(register_1_s0), .A(req), .B(p3s), .C(p7s), .D(p37s), .red(controller_1_red),
    .org(controller_1_org), .n1(controller_1_n1), .resetT(resetT), .n1_2(controller_1_n1_2),
    .n0(controller_1_n0));
  register register_1 (.s1(register_1_s1), .s0(register_1_s0), .n1(controller_1_n1_2), .n0(controller_1_n0));
  LED redL (.in(controller_1_red));
  LED orangeL (.in(controller_1_org));
  LED greenL (.in(controller_1_n1));
endmodule

module controller (
  input  s1,
  input  s0,
  input  A,
  input  B,
  input  C,
  input  D,
  output red,
  output org,
  output n1,
  output resetT,
  output n1_2,
  output n0
);

  wire and_1_out, and_2_out, and_3_out, and_4_out, and_5_out, and_6_out, and_7_out, and_8_out, not_1_out,
       not_2_out;

  not not_1 (not_1_out, s1);
  not not_2 (not_2_out, s0);
  // NOT_Gate not_3 has open pins: in=A, out=open
  // NOT_Gate not_4 has open pins: in=B, out=open
  // NOT_Gate not_5 has open pins: in=C, out=open
  // NOT_Gate not_6 has open pins: in=D, out=open
  and and_1 (and_1_out, not_1_out, not_2_out, A);
  and and_2 (and_2_out, s1, s0, D);
  and and_3 (and_3_out, not_1_out, not_2_out);
  and and_4 (and_4_out, s1, s0, D);
  and and_5 (and_5_out, not_1_out, s0, B);
  and and_6 (and_6_out, s1, not_2_out, C);
  and and_7 (and_7_out, not_1_out, not_2_out, A);
  and and_8 (and_8_out, s1, not_2_out, C);
  or or_1 (red, and_1_out, and_2_out);
  and and_9 (org, not_1_out, s0, B);
  and and_10 (n1, s1, not_2_out, C);
  or or_2 (resetT, and_3_out, and_4_out);
  or or_3 (n1_2, and_5_out, and_6_out);
  or or_4 (n0, and_7_out, and_8_out);
endmodule

module register (
  input  n1,
  input  n0,
  output s1,
  output s0
);

  wire clock_1_out;

  Clock clock_1 (.out(clock_1_out));
  D_Flip_Flop d_ff_1 (.clk(clock_1_out), .D(n1), .Q(s1), .en(1'b1));  // open: Qn, preset, reset
  D_Flip_Flop d_ff_2 (.clk(clock_1_out), .D(n0), .Q(s0), .en(1'b1));  // open: Qn, preset, reset
endmodule
